# Fritzing sketch schematic (saved by Fritzing 0.9.2b)
circuit board: 3.50149cm x 3.27143cm
breadboards: 1

parts:
  S4 = Tilt Switch [package=THT]
  VCC2 = Battery block 9V
  R7 = Resistor [tolerance=±10% resistance=10k package=THT]
  R10 = Resistor [tolerance=±5% resistance=10k package=THT]
  S6 = Tilt Switch [package=THT]
  R11 = Resistor [tolerance=±10% resistance=10k package=THT]
  D2 = Rectifier Diode [part_number=1N4001 package="300 mil [THT]"]
  R9 = Resistor [tolerance=±5% resistance=10k package=THT]
  S5 = Tilt Switch [package=THT]
  U2 = ESP8266 WiFi Module [part_number=ESP8266]

nets:
  N1: S4.Pin_1, D2.anode
  N2: S4.Pin_2, S6.Pin_1
  N3: VCC2.-, R7.Pin_0, R11.Pin_0, S5.Pin_2, U2.GND
  N4: VCC2.+, S6.Pin_2, R9.Pin_0, U2.VCC
  N5: R7.Pin_1, U2.GPIO_15
  N6: R10.Pin_0, U2.GPIO_14
  N7: R10.Pin_1, R11.Pin_1, D2.cathode, U2.CH_PD
  N8: R9.Pin_1, S5.Pin_1, U2.GPIO_13

custom parts:
  ESP8266 WiFi Module: Generic WiFi Module based on the ESP8266 with onboard PCB antenna and UART communications
